// Logisim project Circuitos Sequenciais.circ as structural Verilog: 9 circuits, main circuit RS
module RS (
  input  R,
  input  S,
  output Q,
  output Q_prime
);

  nor nor_1 (Q, R, Q_prime);
  nor nor_2 (Q_prime, Q, S);
endmodule

module RS_Clock (
  input  R,
  input  Clock,
  input  S,
  output Q,
  output Q_prime
);

  wire and_1_out, and_2_out;

  and and_1 (and_1_out, R, Clock);
  and and_2 (and_2_out, Clock, S);
  nor nor_1 (Q, and_1_out, Q_prime);
  nor nor_2 (Q_prime, Q, and_2_out);
endmodule

module D (
  input  Clock,
  input  D,
  output Q,
  output Q_prime
);

  wire and_1_out, and_2_out, not_1_out;

  not not_1 (not_1_out, D);
  and and_1 (and_1_out, not_1_out, Clock);
  and and_2 (and_2_out, Clock, D);
  nor nor_1 (Q, and_1_out, Q_prime);
  nor nor_2 (Q_prime, Q, and_2_out);
endmodule

module JK (
  input  K,
  input  Clock,
  input  J,
  output Q,
  output Q_prime
);

  wire and_1_out, and_2_out;

  and and_1 (and_1_out, Q, K, Clock);
  and and_2 (and_2_out, Clock, J, Q_prime);
  nor nor_1 (Q, and_1_out, Q_prime);
  nor nor_2 (Q_prime, Q, and_2_out);
endmodule

module FlipFlopD (
  input  Clock,
  input  D,
  output Q,
  output Q_prime
);

  D_Flip_Flop d_ff_1 (.clk(Clock), .D(D), .Q(Q), .Qn(Q_prime), .preset(1'b0), .en(1'b1), .reset(1'b0));
endmodule

module FlipFlopJK (
  input  J,
  input  Clock,
  input  K,
  output Q,
  output Q_prime
);

  J_K_Flip_Flop #(.trigger("falling")) j_k_ff_1 (
    .J(J), .clk(Clock), .K(K), .Q(Q), .Qn(Q_prime), .preset(1'b0), .en(1'b1), .reset(1'b0));
endmodule

module FlipFlopJK_Clear (
  input  J,
  input  Clock,
  input  K,
  input  Clear,
  output Q,
  output Q_prime
);

  J_K_Flip_Flop #(.trigger("falling")) j_k_ff_1 (
    .J(J), .clk(Clock), .K(K), .Q(Q), .Qn(Q_prime), .preset(1'b0), .en(1'b1), .reset(Clear));
endmodule

module registrador_paralelo_8_bits (
  input  E7,
  input  E6,
  input  E5,
  input  E4,
  input  E3,
  input  E2,
  input  E1,
  input  E0,
  input  Load,
  output out_10,
  output out_11,
  output out_12,
  output out_13,
  output out_14,
  output out_15,
  output out_16,
  output out_17
);

  wire and_1_out, clock_1_out;

  Clock clock_1 (.out(clock_1_out));
  and and_1 (and_1_out, clock_1_out, Load);
  FlipFlopD flipflopd_1 (.Clock(and_1_out), .D(E7), .Q(out_10));  // open: Q_prime
  FlipFlopD flipflopd_2 (.Clock(and_1_out), .D(E6), .Q(out_11));  // open: Q_prime
  FlipFlopD flipflopd_3 (.Clock(and_1_out), .D(E5), .Q(out_12));  // open: Q_prime
  FlipFlopD flipflopd_4 (.Clock(and_1_out), .D(E4), .Q(out_13));  // open: Q_prime
  FlipFlopD flipflopd_5 (.Clock(and_1_out), .D(E3), .Q(out_14));  // open: Q_prime
  FlipFlopD flipflopd_6 (.Clock(and_1_out), .D(E2), .Q(out_15));  // open: Q_prime
  FlipFlopD flipflopd_7 (.Clock(and_1_out), .D(E1), .Q(out_16));  // open: Q_prime
  FlipFlopD flipflopd_8 (.Clock(and_1_out), .D(E0), .Q(out_17));  // open: Q_prime
endmodule

module registrador_deslocamento (
  input  E7,
  output out_2,
  output out_3,
  output out_4,
  output out_5,
  output out_6
);

  wire clock_1_out;

  Clock clock_1 (.out(clock_1_out));
  FlipFlopD flipflopd_1 (.Clock(clock_1_out), .D(E7), .Q(out_2));  // open: Q_prime
  FlipFlopD flipflopd_2 (.Clock(clock_1_out), .D(out_2), .Q(out_3));  // open: Q_prime
  FlipFlopD flipflopd_3 (.Clock(clock_1_out), .D(out_3), .Q(out_4));  // open: Q_prime
  FlipFlopD flipflopd_4 (.Clock(clock_1_out), .D(out_4), .Q(out_5));  // open: Q_prime
  FlipFlopD flipflopd_5 (.Clock(clock_1_out), .D(out_5), .Q(out_6));  // open: Q_prime
endmodule
